// Logisim project cpu.circ as structural Verilog: 1 circuit, main circuit cpu
module cpu (
  input  [3:0] in_1,
  input  [31:0] in_2
);

  wire ALUOpValid, ALUSrc, and_1_out, Branch, clk, is_op, JAL, Jump, JumpReg, LB, MemToReg, RegDes, RegWrite,
       SLTi, zero;
  wire [3:0] MemMask;
  wire [4:0] instr2, instr3, multiplexer_1_out, multiplexer_2_out;
  wire [5:0] ALUOp, func, opcd_fnc, opcode;
  wire [15:6] instr0;
  wire [31:0] adder_1_out, adder_2_out, DataMem_p5, extended, multiplexer_3_out, multiplexer_4_out,
       multiplexer_6_out, new_PC, PC, rdData2, RegisterFile_p7, result, shifter_1_out, writeData;

  Register #(.width(32)) register_1 (.D(new_PC), .en(1'b1), .clk(clk), .Q(PC), .clr(1'b0));
  Adder #(.width(32)) adder_1 (.a(PC), .b(32'h4), .out(adder_1_out), .cin(1'b0));  // open: cout
  Clock clock_1 (.out(clk));
  // mem InstMem: pin names not known; wires that end beside it: PC, in_1, in_2, clk, {opcode, instr3, instr2, instr0, func}
  Shifter #(.width(32)) shifter_1 (.in(extended), .\dist (5'b00010), .out(shifter_1_out));
  Multiplexer #(.width(5)) multiplexer_1 (.in0(instr2), .in1(instr0[15:11]), .out(multiplexer_1_out), .sel(RegDes));
  Adder #(.width(32)) adder_2 (.a(adder_1_out), .b(shifter_1_out), .out(adder_2_out), .cin(1'b0));  // open: cout
  Multiplexer #(.width(5)) multiplexer_2 (.in0(multiplexer_1_out), .in1({5{1'b1}}), .out(multiplexer_2_out), .sel(JAL));
  Multiplexer #(.width(32)) multiplexer_3 (.in0(writeData), .in1(PC), .out(multiplexer_3_out), .sel(JAL));
  Multiplexer #(.width(32)) multiplexer_4 (
    .in0(adder_1_out), .in1(adder_2_out), .out(multiplexer_4_out), .sel(and_1_out));
  and and_1 (and_1_out, zero, Branch);
  Multiplexer #(.width(32)) multiplexer_5 (
    .in0(multiplexer_4_out), .in1({PC[31:28], instr3, instr2, instr0, func, 2'b00}), .out(new_PC), .sel(Jump));
  SignExtend signextend_1 (.inpt({instr0, func}), .opcode(opcode), .outpt(extended));
  // regfile RegisterFile: pin names not known; wires that end beside it: instr3, instr2, multiplexer_3_out, RegWrite, clk, multiplexer_2_out, RegisterFile_p7, rdData2
  Multiplexer #(.width(32)) multiplexer_6 (.in0(rdData2), .in1(extended), .out(multiplexer_6_out), .sel(ALUSrc));
  ControlUnit controlunit_1 (
    .Opcode(opcode), .Func(func), .ALUSrc(ALUSrc), .RegWrite(RegWrite), .ALUOp(ALUOp),
    .ALUOpValid(ALUOpValid), .MemMask(MemMask), .JAL(JAL), .JumpReg(JumpReg), .RegDest(RegDes), .Jump(Jump),
    .Branch(Branch), .LB(LB), .MemToReg(MemToReg), .SLTi(SLTi));
  aluControl alucontrol_1 (.func(func), .aluOP(ALUOp), .opcd_fnc(opcd_fnc), .is_op(is_op));
  alu alu_1 (
    .rs(RegisterFile_p7), .rt_imm(multiplexer_6_out), .opcd_fnc(opcd_fnc), .shft_amt(instr0[10:6]),
    .is_i(is_op), .result(result), .zero(zero));
  // mem DataMem: pin names not known; wires that end beside it: result, MemMask, rdData2, clk, DataMem_p5
  Multiplexer #(.width(32)) multiplexer_7 (.in0(result), .in1(DataMem_p5), .out(writeData), .sel(MemToReg));

  // Other names for the same wires on the sheet: instr0[5:0] = func; Jinstr[25:0] = {instr3, instr2, instr0, func};
  //   sh_amount[4:0] = instr0[10:6]; instr1[4:0] = instr0[15:11]
endmodule
